# Fritzing sketch esp8266-ldr (saved by Fritzing 0.9.3b)
breadboards: 1

parts:
  U1 = NodeMCU V3.0
  e-radionica_com1 = LM393 LDR breakout [part_number=100027]

nets:
  N1: U1.GND#6, U1.GND#13, U1.GND#16, U1.GND#33, e-radionica_com1.GND
  VIN: U1.Vin, e-radionica_com1.VCC
  N2: U1.A0, e-radionica_com1.AO

custom parts:
  NodeMCU V3.0: ESP8266 based NodeMCU
