# Fritzing sketch esp8266-lcd-i2c (saved by Fritzing 0.9.3b)
breadboards: 1

parts:
  LCM1602_IIC3 = LCM1602 IIC [part_number="LCM1602 IIC" chip_label="LCM1602 IIC" package="DIP (Dual Inline) [THT]"]
  LCD3 = LCD screen
  U3 = NodeMCU V3.0

nets:
  VSS: LCM1602_IIC3.VSS, LCD3.VSS
  VDD: LCM1602_IIC3.VDD, LCD3.VDD
  N1: LCM1602_IIC3.V0, LCD3.V0
  N2: LCM1602_IIC3.RS, LCD3.RS
  N3: LCM1602_IIC3.RW, LCD3.R/W
  N4: LCM1602_IIC3.E, LCD3.E
  N5: LCM1602_IIC3.D0, LCD3.DB0
  N6: LCM1602_IIC3.D1, LCD3.DB1
  N7: LCM1602_IIC3.D2, LCD3.DB2
  N8: LCM1602_IIC3.D3, LCD3.DB3
  N9: LCM1602_IIC3.D4, LCD3.DB4
  N10: LCM1602_IIC3.D5, LCD3.DB5
  N11: LCM1602_IIC3.D6, LCD3.DB6
  N12: LCM1602_IIC3.D7, LCD3.DB7
  N13: LCM1602_IIC3.A, LCD3.LED+
  N14: LCM1602_IIC3.K, LCD3.LED-
  N15: LCM1602_IIC3.GND, U3.GND#6, U3.GND#13, U3.GND#16, U3.GND#33
  VCC: LCM1602_IIC3.VCC, U3.Vin
  N16: LCM1602_IIC3.SDA, U3.D2
  N17: LCM1602_IIC3.SCL, U3.D1
  N18: LCM1602_IIC3.LED_A, LCM1602_IIC3.LED_B

custom parts:
  LCM1602 IIC: I2C-Module to use a 1602 or 2004 LCD on with the wire.h libory Serial LCD Modul
  NodeMCU V3.0: ESP8266 based NodeMCU
